# Fritzing sketch Wiring (saved by Fritzing 1.0.4)

parts:
  M1 = gy9250
  Mod1 = Raspberry Pi Pico W

nets:
  N1: M1.pin1, Mod1.pin_36
  N2: M1.pin2, M1.pin7, Mod1.pin_38, Mod1.pin_42
  N3: M1.pin3, Mod1.pin_2
  N4: M1.pin4, Mod1.pin_1

custom parts:
  gy9250: MPU-9250 module (three-axis gyroscope + three-axis acceleration + three-axis magnetic field). The generic model from ebay et. al. rather than the Sparkfun version.
  Raspberry Pi Pico W: Raspberry Pi Pico W. Based around the RP2040 microcontroller the Pico W is a low cost microcontroller device bringing Raspberry Pi quality, cost, and easy of use to the microcontroller space. The areas marked KEEPOUT in pcb silkscreen should not have traces running through them to avoid shorts on a soldered in module!
